// Logisim project TIS.circ as structural Verilog: 3 circuits, main circuit main
module main (
);

  ROM rom_1 ();  // open: addr, data
endmodule

module Tis_Node_Arch (
);

  Register register_1 ();  // open: D, en, clk, Q, clr
endmodule

module Tis_NodeComunication_Arch (
);

  wire [7:0] register_1_q;

  Register register_1 (.Q(register_1_q));  // open: D, en, clk, clr
endmodule
